# Fritzing sketch StogieSaver (saved by Fritzing 0.8.0b)
breadboards: 1

parts:
  Teensy_3_1 = Teensy 3.0
  DHT1 = DHT11 Humitidy and Temperature Sensor
  R1 = Resistor [tolerance=±5% resistance=220 package="0805 [SMD]"]

nets:
  GND: Teensy_3_1.GND, DHT1.GND
  N1: Teensy_3_1.D1, DHT1.DATA, R1.Pin_1
  3V3: Teensy_3_1.D12, Teensy_3_1.VBat, Teensy_3_1.3V3, DHT1.VDD, R1.Pin_0
  N2: Teensy_3_1.Reset, Teensy_3_1.D13

custom parts:
  DHT11 Humitidy and Temperature Sensor: DHT11 Humidity and Temperature Sensor
